# Fritzing sketch car_stable_1 (saved by Fritzing 0.9.3b)

parts:
  Часть1 = Arduino Uno (Rev3) - ICSP
  Часть2 = NRF24L01+ Breakout Board
  U1 = L298 [package=multiwatt15]
  M1 = DC Motor  # not connected
  M2 = DC Motor  # not connected
  M3 = DC Motor  # not connected
  M4 = DC Motor  # not connected
  J1 = Basic Servo
  hc-sr2 = hc-sr04
  hc-sr1 = hc-sr04
  VCC1 = 4 x AAA Battery Mount  # not connected

nets:
  N1: Часть1.A0, hc-sr1.Trig
  N2: Часть1.A1, hc-sr1.Echo
  N3: Часть1.A2, hc-sr2.Trig
  N4: Часть1.A3, hc-sr2.Echo
  N5: Часть1.A5/SCL, Часть2.CS
  N6: Часть1.ICSP_MISO, Часть1.D12/MISO, Часть2.MISO
  N7: Часть1.D8, U1.IN2
  N8: Часть1.D9_PWM, J1.pulse
  N9: Часть1.D10_PWM/SS, U1.ENA
  N10: Часть1.D11_PWM/MOSI, Часть2.MOSI
  N11: Часть1.D13/SCK, Часть2.SCK
  N12: Часть1.D3_PWM, Часть2.CE
  N13: Часть1.D4, U1.IN4
  N14: Часть1.D5_PWM, U1.IN1
  N15: Часть1.D6_PWM, U1.ENB
  N16: Часть1.D7, U1.IN3
